# Fritzing sketch RCCar_Sketch (saved by Fritzing 0.9.3b)
breadboards: 1

parts:
  パーツ1 = Arduino Pro Mini (5V)
  M1 = DC Motor
  M2 = DC Motor
  M3 = DC Motor
  M4 = DC Motor
  J1 = Basic Servo
  J2 = Basic Servo
  パーツ2 = Motor Driver 1A Dual TB6612FNG
  パーツ3 = Motor Driver 1A Dual TB6612FNG
  BAT1 = Battery Holders [package=battery-aa-kit]
  BAT2 = Battery Holders [package=battery-aa-kit]
  BAT4 = Battery Holders [package=battery-aa-kit]
  BAT5 = Battery Holders [package=battery-aa-kit]
  W2 = ESPr Developer [package="DIP (Dual Inline) [THT]"]
  U1 = Voltage Regulator - 5V [package="DPak [SMD]"]
  VCC1 = 4 x AAA Battery Mount
  BAT3 = Battery Holders [package=battery-aa-kit]

nets:
  N1: パーツ1.A4, W2.IO4
  N2: パーツ1.A5, W2.IO5
  N3: パーツ1.RAW, W2.VOUT
  N4: パーツ1.GND, W2.GND#12
  N5: パーツ1.A3, パーツ3.BIN2
  N6: パーツ1.A2, パーツ3.BIN1
  N7: パーツ1.A1, パーツ3.AIN1
  N8: パーツ1.A0, パーツ3.AIN2
  N9: パーツ1.SCK, パーツ2.BIN2
  N10: パーツ1.MISO, パーツ2.BIN1
  N11: パーツ1.MOSI, J2.pulse
  N12: パーツ1.D10, J1.pulse
  N13: パーツ1.D9, パーツ3.PWMB
  N14: パーツ1.D8, パーツ2.AIN1
  N15: パーツ1.D7, パーツ2.AIN2
  N16: パーツ1.D6, パーツ3.PWMA
  N17: パーツ1.D5, パーツ2.PWMB
  N18: パーツ1.D3, パーツ2.PWMA
  N19: M1.pin_1, パーツ3.B01
  N20: M1.pin_2, パーツ3.B02
  N21: M2.pin_1, パーツ3.A02
  N22: M2.pin_2, パーツ3.A01
  N23: M3.pin_1, パーツ2.B01
  N24: M3.pin_2, パーツ2.B02
  N25: M4.pin_1, パーツ2.A02
  N26: M4.pin_2, パーツ2.A01
  GND: J1.gnd, J2.gnd, パーツ2.GND, パーツ3.GND, BAT1.-, W2.GND#9, U1.GND, VCC1.-
  VCC: J1.vcc, J2.vcc, U1.input_voltage
  VCC_2: パーツ2.VCC, パーツ2.STBY, パーツ3.VCC, パーツ3.STBY, W2.VIN, VCC1.+
  N27: パーツ2.VM, パーツ3.VM, BAT5.+, U1.output_voltage
  N28: BAT1.+, BAT2.-
  N29: BAT2.+, BAT3.-
  N30: BAT4.+, BAT5.-
  N31: BAT4.-, BAT3.+
